# Fritzing sketch sauf (saved by Fritzing 0.9.9b)
breadboards: 1

parts:
  R1 = Resistor [tolerance=±5% resistance=10k package="2010 [SMD]"]
  RFID-Modul = RFID-RC522-v2
  LED1 = LED - 5mm [color="Green (565nm)" current=0.030 package="5 mm [THT]"]
  Raspberry_Pi_1 = Raspberry Pi 3 [part_number=RPI-3-V1.2]
  PiCamera_an_CSI = Rasberry Pi NIOR Camera [chip_label=IC package="DIP (Dual Inline) [THT]"]  # not connected
  LED2 = LED - 5mm [color="Red (633nm)" current=0.030 package="5 mm [THT]"]

nets (from the breadboard view):
  N1: R1.Pin_0, LED1.anode
  N2: R1.Pin_1, RFID-Modul.MOSI, Raspberry_Pi_1.GND
  N3: RFID-Modul.SDA, Raspberry_Pi_1.3v3
  N4: RFID-Modul.SCK, RFID-Modul.3.3V, Raspberry_Pi_1.GPIO8, Raspberry_Pi_1.GPIO25
  N5: RFID-Modul.IRQ, RFID-Modul.RST, Raspberry_Pi_1.GPIO9, Raspberry_Pi_1.GPIO11
  N6: RFID-Modul.GND, Raspberry_Pi_1.GPIO10
  N7: LED1.cathode, Raspberry_Pi_1.GPIO4, LED2.anode
  N8: Raspberry_Pi_1.GPIO17, LED2.cathode

custom parts:
  RFID-RC522-v2: A simple China made RFID-RC522 Reader; do check the pin labels, as this is a MFRC522 based clone.
  Rasberry Pi NIOR Camera: Camera
